// Digital circuit CP263_Lab_01_01 Wire Connection.dig as structural Verilog
module CP263_Lab_01_01_Wire_Connection (
  input  A,
  input  B,
  input  C,
  input  D,
  output [3:0] Z
);

  Seven_Seg_Hex seven_seg_hex_1 (.d({D, C, B, A}), .dp(1'b0));

  assign Z = {D, C, B, A};

  // Notes on the sheet:
  //   CP263 Lab 01_01 Wire Connection
endmodule
