// Digital circuit CP263_Lab_01_02 Logic Gate.dig as structural Verilog
module CP263_Lab_01_02_Logic_Gate (
  input  A,
  input  B,
  output And,
  output Or,
  output Nand,
  output Xor,
  output Nor,
  output Xnor
);

  and and_1 (And, A, B);
  or or_1 (Or, A, B);
  nand nand_1 (Nand, A, B);
  nor nor_1 (Nor, A, B);
  xor xor_1 (Xor, A, B);
  xnor xnor_1 (Xnor, A, B);

  // Notes on the sheet:
  //   CP263 Lab 01_02 Logic Gate
endmodule
