// Digital circuit CP263_Lab_01_03 Clock Gate.dig as structural Verilog
module CP263_Lab_01_03_Clock_Gate (
  input  A,
  input  C1,
  output Z
);

  and and_1 (Z, A, C1);

  // Notes on the sheet:
  //   CP263 Lab 01_03 Clock Gate
endmodule
