// Digital circuit CP263_Lab_01_04 Dual Clock.dig as structural Verilog
module CP263_Lab_01_04_Dual_Clock (
  input  C1,
  input  C2,
  output Z
);

  and and_1 (Z, C1, C2);

  // Notes on the sheet:
  //   C1: Hz: 2
  //   CP263 Lab 01_04 Dual Clock
endmodule
