// Digital circuit CP263_Lab_02_01_XOR_SOP.dig as structural Verilog
module CP263_Lab_02_01_XOR_SOP (
  input  A,
  input  B,
  output Output
);

  wire and_1_out, and_2_out, not_1_out, not_2_out;

  not not_1 (not_1_out, A);
  not not_2 (not_2_out, B);
  and and_1 (and_1_out, not_1_out, B);
  and and_2 (and_2_out, A, not_2_out);
  or or_1 (Output, and_1_out, and_2_out);

  // Notes on the sheet:
  //   CP263 Lab 02_01 XOR (Sum Of Products)
  //   F = (~A.B) + (A.~B)
  //   ~A
  //   A
  //   B
  //   ~B
  //   ~A.B
  //   A.~B
endmodule
