// Digital circuit CP263_Lab_02_02_XOR_POS.dig as structural Verilog
module CP263_Lab_02_02_XOR_POS (
  input  A,
  input  B,
  output Output
);

  wire not_1_out, not_2_out, or_1_out, or_2_out;

  not not_1 (not_1_out, A);
  not not_2 (not_2_out, B);
  or or_1 (or_1_out, not_1_out, not_2_out);
  or or_2 (or_2_out, A, B);
  and and_1 (Output, or_2_out, or_1_out);

  // Notes on the sheet:
  //   CP263 Lab 02_02 XOR (Product of Sum)
  //   F = (A + B) . (~A + ~B)
  //   A
  //   ~A
  //   B
  //   ~B
  //   A+B
  //   ~A+~B
endmodule
