// Digital circuit CP263_Lab_02_03_FullAdder_SOP.dig as structural Verilog
module CP263_Lab_02_03_FullAdder_SOP (
  input  A,
  input  B,
  input  Cin,
  output Sum,
  output Cout
);

  wire and_1_out, and_2_out, xor_1_out;

  xor xor_1 (xor_1_out, A, B);
  and and_1 (and_1_out, B, A);
  xor xor_2 (Sum, xor_1_out, Cin);
  and and_2 (and_2_out, xor_1_out, Cin);
  or or_1 (Cout, and_2_out, and_1_out);

  // Notes on the sheet:
  //   CP263 Lab 02_03 Full Adder (Sum of Products)
  //   SOP_Sum = (A ^ B) ^ C_in
  //   SOP_Cout = A.B + C_in.(A ^ B)
  //   Note : ^ = XOR = ~A.B + A.~B
  //   A ^ B
  //   C_in
  //   AB
  //   (A ^ B) ^ C_in
  //   (A ^ B) . C_in
  //   AB + (A ^ B) . C_in
endmodule
