// Digital circuit CP263_Lab_02_03_FullAdder_SOP_Fixed.dig as structural Verilog
module CP263_Lab_02_03_FullAdder_SOP_Fixed (
  input  A,
  input  B,
  input  Cin,
  output Sum,
  output Cout
);

  wire and_1_out, and_2_out, and_3_out, and_4_out, and_5_out, and_6_out, and_7_out, and_8_out, and_9_out,
       and_10_out, not_1_out, not_2_out, not_3_out, or_1_out, or_2_out, or_3_out;

  not not_1 (not_1_out, A);
  not not_2 (not_2_out, B);
  not not_3 (not_3_out, Cin);
  and and_1 (and_1_out, not_1_out, B);
  and and_2 (and_2_out, A, not_2_out);
  and and_3 (and_3_out, A, B);
  and and_4 (and_4_out, not_1_out, not_2_out);
  and and_5 (and_5_out, A, B);
  and and_6 (and_6_out, not_1_out, B);
  and and_7 (and_7_out, A, not_2_out);
  or or_1 (or_1_out, and_1_out, and_2_out);
  or or_2 (or_2_out, and_3_out, and_4_out);
  or or_3 (or_3_out, and_6_out, and_7_out);
  and and_8 (and_8_out, not_3_out, or_1_out);
  and and_9 (and_9_out, Cin, or_2_out);
  and and_10 (and_10_out, or_3_out, Cin);
  or or_4 (Sum, and_8_out, and_9_out);
  or or_5 (Cout, and_5_out, and_10_out);

  // Notes on the sheet:
  //   CP263 Lab 02_03 Full Adder (Sum of Products)
  //   SOP_Sum = (A ^ B) ^ C_in = ~Cin(~A.B + A.~B) + Cin(A.B + ~A.~B)
  //   SOP_Cout = A.B + C_in.(A ^ B)
  //   Note : ^ = XOR = ~A.B + A.~B
  //   ~A
  //   B
  //   A
  //   ~B
  //   Cin
  //   ~Cin
endmodule
