// Digital circuit CP263_Lab_02_04_FullAdder_POS.dig as structural Verilog
module CP263_Lab_02_04_FullAdder_POS (
  input  A,
  input  B,
  input  Cin,
  output Sum,
  output Cout
);

  wire not_1_out, not_2_out, not_3_out, or_1_out, or_2_out, or_3_out, or_4_out, or_5_out, or_6_out, or_7_out;

  not not_1 (not_1_out, A);
  not not_2 (not_2_out, B);
  not not_3 (not_3_out, Cin);
  or or_1 (or_1_out, A, B, Cin);
  or or_2 (or_2_out, A, not_2_out, not_3_out);
  or or_3 (or_3_out, not_1_out, B, not_3_out);
  or or_4 (or_4_out, not_1_out, not_2_out, Cin);
  or or_5 (or_5_out, A, B);
  or or_6 (or_6_out, A, Cin);
  or or_7 (or_7_out, B, Cin);
  and and_1 (Sum, or_1_out, or_2_out, or_3_out, or_4_out);
  and and_2 (Cout, or_5_out, or_6_out, or_7_out);

  // Notes on the sheet:
  //   CP263 Lab 02_04 Full Adder (Product of Sum)
  //   POS_ Sum = (A+B+Cin).(A+~B+~Cin).(~A+B+~Cin).(~A+~B+Cin)
  //   POS_ Cout = (A+B).(A+Cin).(B+Cin)
  //   Note : ^ = XOR = ~A.B + A.~B
  //   A
  //   ~A
  //   B
  //   ~B
  //   C_in
  //   ~C_in
  //   !A
  //   !B
  //   C
  //   !C
  //   !C_in
  //   A+B+C_in
  //   A+~B+~C_in
  //   ~A+B+~C_in
  //   ~A+~B+C_in
  //   A+B
  //   A+C_in
  //   B+C_in
  //   POS_Sum
  //   POS_Cout
endmodule
