// Digital circuit CP263_Lab_02_05_Comparator_SOP.dig as structural Verilog
module CP263_Lab_02_05_Comparator_SOP (
  input  A,
  input  B,
  input  C,
  input  D,
  output Z1,
  output Z2,
  output Z3
);

  wire and_1_out, and_2_out, and_3_out, and_4_out, and_5_out, and_6_out, and_7_out, and_8_out, and_9_out,
       and_10_out, and_11_out, and_12_out, and_13_out, and_14_out, and_16_out, not_1_out, not_2_out,
       not_3_out, not_4_out, or_1_out, or_2_out, or_3_out, xor_1_out, xor_2_out, xor_3_out, xor_4_out;

  not not_1 (not_1_out, A);
  not not_2 (not_2_out, B);
  not not_3 (not_3_out, C);
  not not_4 (not_4_out, D);
  and and_1 (and_1_out, not_3_out, not_4_out);
  xor xor_1 (xor_1_out, A, B);
  and and_2 (and_2_out, A, B);
  xor xor_2 (xor_2_out, C, D);
  and and_3 (and_3_out, A, not_3_out);
  xor xor_3 (xor_3_out, B, D);
  and and_4 (and_4_out, not_1_out, not_2_out);
  xor xor_4 (xor_4_out, C, D);
  and and_5 (and_5_out, not_2_out, D);
  and and_6 (and_6_out, not_1_out, B);
  and and_7 (and_7_out, not_2_out, not_4_out);
  and and_8 (and_8_out, B, D);
  and and_9 (and_9_out, not_1_out, not_3_out);
  and and_10 (and_10_out, A, C);
  or or_1 (or_1_out, and_7_out, and_8_out);
  or or_2 (or_2_out, and_9_out, and_10_out);
  and and_11 (and_11_out, and_1_out, xor_1_out);
  and and_12 (and_12_out, and_2_out, xor_2_out);
  and and_13 (and_13_out, and_3_out, xor_3_out);
  and and_14 (and_14_out, and_4_out, xor_4_out);
  or or_3 (or_3_out, and_5_out, and_6_out);
  and and_15 (Z3, or_1_out, or_2_out);
  and and_16 (and_16_out, or_3_out, C);
  or or_4 (Z1, and_11_out, and_12_out, and_13_out);
  or or_5 (Z2, and_14_out, and_16_out);

  // Notes on the sheet:
  //   Z1: N1 > N2
  //   Z2: N1 < N2
  //   Z3: N1 = N2
  //   A
  //   ~A
  //   B
  //   ~B
  //   C
  //   ~C
  //   D
  //   ~D
  //   CP263 Lab 02_05 Comparator (Sum of Products)
  //   Z1 = ~C.~D.(A ^ B) + A.~C.(B ^ D) + A.B.(C ^ D)
  //   Z2 = ~A.~B.(C ^ D) + C.(~B.D + ~A.B)
  //   Z3 = (B *^ D).(C *^ A)
  //   Note that * means XNOR Gate
  //   A ^ B
  //   A.B
  //   C ^ D
  //   A.~C
  //   B ^ D
  //   ~A.~B
  //   ~B.D
  //   ~A.B
  //   ~B.~D
  //   B.D
  //   ~A.~C
  //   A.C
  //   ~C~D
  //   ~C~D.(A ^ B)
  //   AB.(C ^ D)
  //   A.~C.(B ^ D)
  //   (~B.D) + (~A.B)
  //   (B *^ D) . (A *^ C) [Abbrev.]
  //   (~A.~B) . (C ^ D)
  //   C . ((~B.D) + (~A.B))
endmodule
