// Digital circuit CP263_Lab_02_06_Comparator_POS.dig as structural Verilog
module CP263_Lab_02_06_Comparator_POS (
  input  A,
  input  B,
  input  C,
  input  D,
  output Z1,
  output Z2,
  output Z3
);

  wire not_1_out, not_2_out, not_3_out, not_4_out, or_1_out, or_2_out, or_3_out, or_4_out, or_5_out,
       or_6_out, or_7_out, or_8_out, or_9_out, or_10_out, or_11_out, or_12_out, or_13_out, or_14_out;

  not not_1 (not_1_out, A);
  not not_2 (not_2_out, B);
  not not_3 (not_3_out, C);
  not not_4 (not_4_out, D);
  or or_1 (or_1_out, A, B);
  or or_2 (or_2_out, not_3_out, not_4_out);
  or or_3 (or_3_out, A, not_3_out);
  or or_4 (or_4_out, A, not_4_out);
  or or_5 (or_5_out, B, not_3_out);
  or or_6 (or_6_out, not_1_out, not_2_out);
  or or_7 (or_7_out, C, D);
  or or_8 (or_8_out, not_1_out, D);
  or or_9 (or_9_out, not_1_out, C);
  or or_10 (or_10_out, not_2_out, C);
  or or_11 (or_11_out, not_1_out, C);
  or or_12 (or_12_out, not_2_out, D);
  or or_13 (or_13_out, B, not_4_out);
  or or_14 (or_14_out, A, not_3_out);
  and and_1 (Z1, or_1_out, or_2_out, or_3_out, or_4_out, or_5_out);
  and and_2 (Z2, or_6_out, or_7_out, or_8_out, or_9_out, or_10_out);
  and and_3 (Z3, or_11_out, or_12_out, or_13_out, or_14_out);

  // Notes on the sheet:
  //   A
  //   ~A
  //   B
  //   ~B
  //   C
  //   ~C
  //   D
  //   ~D
  //   A+B
  //   ~C+~D
  //   A+~C
  //   A+~D
  //   B+~C
  //   ~A+~B
  //   C+D
  //   ~A+D
  //   ~A+C
  //   ~B+C
  //   ~B+D
  //   B+~D
  //   CP263 Lab 02_06 Comparator (Product of Sums)
  //   Using K-Map
  //   Z1 = (A+B).(~C+~D).(A+~C).(A+~D).(B+~C)
  //   Z2 = (~A+~B).(C+D).(~A+D).(~A+C).(~B+C)
  //   Z3 = (~A+C).(~B+D).(B+~D).(A+~C)
endmodule
