// Digital circuit CP263_Lab_02_07_Multiplexer_SOP.dig as structural Verilog
module CP263_Lab_02_07_Multiplexer_SOP (
  input  X1,
  input  X0,
  input  Selector,
  output Z
);

  wire and_1_out, and_2_out, not_1_out;

  and and_1 (and_1_out, X1, Selector);
  not not_1 (not_1_out, Selector);
  and and_2 (and_2_out, not_1_out, X0);
  or or_1 (Z, and_1_out, and_2_out);

  // Notes on the sheet:
  //   CP263 Lab 02_07 Multiplexer 2:1 (Sum of Products)
  //   Z = X_0.~S + X_1.S
endmodule
