// Digital circuit CP263_Lab_02_08_Multiplexer_POS.dig as structural Verilog
module CP263_Lab_02_08_Multiplexer_POS (
  input  X0,
  input  Selector,
  input  X1,
  output Z
);

  wire not_1_out, or_1_out, or_2_out;

  or or_1 (or_1_out, X0, Selector);
  not not_1 (not_1_out, Selector);
  or or_2 (or_2_out, not_1_out, X1);
  and and_1 (Z, or_1_out, or_2_out);

  // Notes on the sheet:
  //   CP263 Lab 02_08 Multiplexer (Product of Sum)
  //   Z = (X_0 + S).(X_1 + ~S)
endmodule
