// Digital circuit CP263_Lab_03_03_Binary_Encoder.dig as structural Verilog
module CP263_Lab_03_03_Binary_Encoder (
  input  [1:0] Selector,
  input  [3:0] In,
  output [3:0] Output
);

  wire and_1_out, and_2_out, and_3_out, and_4_out, and_5_out, and_6_out, and_7_out, and_8_out, and_9_out,
       and_10_out, and_11_out, and_12_out, and_13_out, and_14_out, and_15_out, and_16_out, and_17_out,
       and_18_out, and_19_out, and_20_out, and_21_out, and_22_out, and_23_out, and_24_out, and_25_out,
       and_26_out, and_27_out, and_28_out, and_29_out, and_30_out, C0, C1, C2, E0, E1, E2, E3, N0, N1, N2,
       N3, not_1_out, not_2_out, not_3_out, not_4_out, not_5_out, not_6_out, not_7_out, not_8_out, not_9_out,
       not_10_out, not_11_out, not_12_out, not_13_out, not_14_out, not_15_out, not_16_out, not_17_out,
       not_18_out, not_19_out, not_20_out, not_21_out, not_22_out, not_23_out, not_24_out, not_25_out, P1,
       P2, P3;

  not not_1 (not_1_out, In[0]);
  not not_2 (not_2_out, In[1]);
  not not_3 (not_3_out, In[1]);
  or or_1 (C2, In[2], In[3]);
  and and_1 (and_1_out, not_1_out, In[1], In[2]);
  and and_2 (and_2_out, In[0], In[2]);
  and and_3 (and_3_out, In[0], not_2_out, In[2]);
  and and_4 (and_4_out, In[1], In[2]);
  and and_5 (and_5_out, In[0], not_3_out, In[2]);
  and and_6 (and_6_out, In[0], In[1]);
  or or_2 (E3, and_1_out, and_2_out, In[3]);
  not not_4 (not_4_out, In[1]);
  or or_3 (P3, and_3_out, and_4_out, In[3]);
  or or_4 (N3, and_5_out, and_6_out, In[3]);
  not not_5 (not_5_out, In[2]);
  Multiplexer #(.Bits(4), .Selector_Bits(2)) multiplexer_1 (
    .sel(Selector), .in_0({E3, E2, E1, E0}), .in_1({In[3], C2, C1, C0}), .in_2({P3, P2, P1, In[0]}),
    .in_3({N3, N2, N1, N0}), .out(Output));
  not not_6 (not_6_out, In[0]);
  and and_7 (and_7_out, In[1], not_5_out);
  and and_8 (and_8_out, not_4_out, In[2]);
  not not_7 (not_7_out, In[1]);
  or or_5 (C1, and_7_out, and_8_out);
  not not_8 (not_8_out, In[0]);
  not not_9 (not_9_out, In[0]);
  not not_10 (not_10_out, In[1]);
  not not_11 (not_11_out, In[2]);
  and and_9 (and_9_out, not_6_out, not_7_out, In[2]);
  and and_10 (and_10_out, not_6_out, In[1], not_11_out);
  and and_11 (and_11_out, In[0], not_11_out);
  not not_12 (not_12_out, In[2]);
  and and_12 (and_12_out, not_8_out, In[2]);
  and and_13 (and_13_out, In[1], In[2]);
  and and_14 (and_14_out, In[0], not_10_out, not_12_out);
  and and_15 (and_15_out, not_9_out, In[2]);
  and and_16 (and_16_out, In[1], In[2]);
  or or_6 (E2, and_9_out, and_10_out, and_11_out);
  not not_13 (not_13_out, In[0]);
  not not_14 (not_14_out, In[1]);
  or or_7 (N2, and_14_out, and_15_out, and_16_out);
  and and_17 (and_17_out, not_13_out, In[1]);
  and and_18 (and_18_out, In[0], not_14_out);
  or or_8 (P2, and_12_out, and_13_out, In[3]);
  not not_15 (not_15_out, In[0]);
  or or_9 (C0, and_17_out, and_18_out);
  not not_16 (not_16_out, In[1]);
  not not_17 (not_17_out, In[0]);
  not not_18 (not_18_out, In[1]);
  and and_19 (and_19_out, In[0], In[1]);
  and and_20 (and_20_out, not_15_out, not_16_out);
  or or_10 (E1, and_19_out, and_20_out);
  not not_19 (not_19_out, In[1]);
  not not_20 (not_20_out, In[2]);
  and and_21 (and_21_out, not_17_out, In[1]);
  and and_22 (and_22_out, In[0], not_18_out, In[2]);
  and and_23 (and_23_out, In[0], not_19_out, In[2]);
  and and_24 (and_24_out, In[1], not_20_out);
  or or_11 (N1, and_21_out, and_22_out, In[3]);
  not not_21 (not_21_out, In[0]);
  or or_12 (P1, and_23_out, and_24_out, In[3]);
  not not_22 (not_22_out, In[1]);
  not not_23 (not_23_out, In[2]);
  and and_25 (and_25_out, not_21_out, In[1], not_23_out);
  and and_26 (and_26_out, not_21_out, In[1], In[2]);
  and and_27 (and_27_out, not_21_out, not_22_out);
  not not_24 (not_24_out, In[1]);
  not not_25 (not_25_out, In[2]);
  or or_13 (E0, and_25_out, and_26_out, and_27_out);
  and and_28 (and_28_out, In[0], not_24_out, not_25_out);
  and and_29 (and_29_out, In[0], not_24_out, In[2]);
  and and_30 (and_30_out, In[0], In[1]);
  or or_14 (N0, and_28_out, and_29_out, and_30_out);

  // Other names for the same wires on the sheet: T1[3:0] = {In[3], C2, C1, C0}; T0[3:0] = {E3, E2, E1, E0};
  //   D0 = In[0]; P0 = In[0]; T2[3:0] = {P3, P2, P1, In[0]}; D1 = In[1]; D2 = In[2]; C3 = In[3]; D3 = In[3];
  //   T3[3:0] = {N3, N2, N1, N0}
endmodule
