// Digital circuit lab3.4.dig as structural Verilog
module lab3_4 (
  input  [6:0] In,
  output [6:0] Output
);

  wire C1, C2, C3, decoder_1_out_0;
  wire [6:0] decoder_1_out_6;

  xor xor_1 (C1, In[3], In[2], In[1], In[0]);
  xor xor_2 (C2, In[5], In[4], In[1], In[0]);
  LED led_1 (.in(decoder_1_out_0));
  Decoder #(.Selector_Bits(3)) decoder_1 (
    .sel({C1, C2, C3}), .out_0(decoder_1_out_0), .out_1(decoder_1_out_6[6]), .out_2(decoder_1_out_6[5]),
    .out_3(decoder_1_out_6[4]), .out_4(decoder_1_out_6[3]), .out_5(decoder_1_out_6[2]),
    .out_6(decoder_1_out_6[1]), .out_7(decoder_1_out_6[0]));
  xor xor_3 (C3, In[6], In[4], In[2], In[0]);
  assign Output = In ^ decoder_1_out_6;  // XOr xor_4, 7 bits wide

  // Other names for the same wires on the sheet: M4 = In[0]; M3 = In[1]; M2 = In[2]; P3 = In[3]; M1 = In[4];
  //   P2 = In[5]; P1 = In[6]
endmodule
