// Digital circuit CP263_Lab_05_02_Glitch_02.dig as structural Verilog
module CP263_Lab_05_02_Glitch_02 (
  input  A,
  input  B,
  input  C,
  input  D,
  input  E,
  output Before,
  output After
);

  wire K1, K2, K3, K4, K5, m0, m1, m3, m4, m7, m11, m12, m15, m16, m17, m20, m28, not_1_out, not_2_out,
       not_3_out, not_4_out, not_5_out, not_6_out, not_7_out, not_8_out, not_9_out, not_10_out, not_11_out,
       not_12_out, not_13_out, not_14_out, not_15_out, not_16_out, not_17_out, not_18_out, not_19_out,
       not_20_out, not_21_out, not_22_out, not_23_out, not_24_out, not_25_out, not_26_out, not_27_out,
       not_28_out, not_29_out, not_30_out, not_31_out, not_32_out, not_33_out, not_34_out, not_35_out,
       not_36_out, or_2_out, or_3_out, or_4_out;

  not not_1 (not_1_out, A);
  not not_2 (not_2_out, B);
  not not_3 (not_3_out, C);
  not not_4 (not_4_out, D);
  not not_5 (not_5_out, E);
  not not_6 (not_6_out, A);
  not not_7 (not_7_out, B);
  not not_8 (not_8_out, C);
  not not_9 (not_9_out, D);
  not not_10 (not_10_out, A);
  not not_11 (not_11_out, B);
  not not_12 (not_12_out, C);
  and and_1 (m0, not_1_out, not_2_out, not_3_out, not_4_out, not_5_out);
  and and_2 (m1, not_6_out, not_7_out, not_8_out, not_9_out, E);
  and and_3 (m3, not_10_out, not_11_out, not_12_out, D, E);
  and and_4 (K1, C, ~D, ~E);  // And
  and and_5 (K3, ~A, D, E);  // And
  and and_6 (K2, ~B, ~C, ~D);  // And
  and and_7 (K4, ~B, ~D, ~E);  // And
  not not_13 (not_13_out, A);
  not not_14 (not_14_out, B);
  not not_15 (not_15_out, D);
  not not_16 (not_16_out, E);
  not not_17 (not_17_out, A);
  not not_18 (not_18_out, B);
  not not_19 (not_19_out, A);
  not not_20 (not_20_out, C);
  and and_8 (m4, not_13_out, not_14_out, C, not_15_out, not_16_out);
  and and_9 (m7, not_17_out, not_18_out, C, D, E);
  and and_10 (m11, not_19_out, B, not_20_out, D, E);
  and and_11 (K5, ~A, ~B, ~C, E);  // And
  not not_21 (not_21_out, A);
  not not_22 (not_22_out, D);
  not not_23 (not_23_out, E);
  not not_24 (not_24_out, A);
  not not_25 (not_25_out, B);
  not not_26 (not_26_out, C);
  not not_27 (not_27_out, D);
  not not_28 (not_28_out, E);
  and and_12 (m12, not_21_out, B, C, not_22_out, not_23_out);
  and and_13 (m15, not_24_out, B, C, D, E);
  and and_14 (m16, A, not_25_out, not_26_out, not_27_out, not_28_out);
  or or_1 (After, K1, K2, K3, K4, K5);
  not not_29 (not_29_out, B);
  not not_30 (not_30_out, C);
  not not_31 (not_31_out, D);
  not not_32 (not_32_out, B);
  not not_33 (not_33_out, D);
  not not_34 (not_34_out, E);
  not not_35 (not_35_out, D);
  not not_36 (not_36_out, E);
  and and_15 (m17, A, not_29_out, not_30_out, not_31_out, E);
  and and_16 (m20, A, not_32_out, C, not_33_out, not_34_out);
  and and_17 (m28, A, B, C, not_35_out, not_36_out);
  or or_2 (or_2_out, m0, m1, m3, m4);
  or or_3 (or_3_out, m7, m11, m12, m15);
  or or_4 (or_4_out, m16, m17, m20, m28);
  or or_5 (Before, or_2_out, or_3_out, or_4_out);
endmodule

/* Test case T1:
A B C D E Before After
0 0 0 0 1 1 1
0 0 0 1 1 1 1
0 0 0 0 1 1 1
0 0 1 1 1 1 1
0 0 0 0 1 1 1
0 1 0 1 1 1 1
0 0 0 0 1 1 1
0 1 1 1 1 1 1
0 0 0 0 1 1 1
1 0 0 0 1 1 1
0 0 0 1 1 1 1
0 0 0 0 1 1 1
0 0 0 1 1 1 1
1 0 0 0 1 1 1
0 0 1 0 0 1 1
0 0 1 1 1 1 1
0 0 1 0 0 1 1
0 1 1 0 0 1 1
0 0 1 0 0 1 1
0 1 1 1 1 1 1
0 0 1 0 0 1 1
1 0 1 0 0 1 1
0 0 1 0 0 1 1
1 1 1 0 0 1 1
0 0 1 1 1 1 1
0 0 0 0 1 1 1
0 0 1 1 1 1 1
0 0 1 0 0 1 1
0 0 1 1 1 1 1
0 1 1 0 0 1 1
0 0 1 1 1 1 1
1 0 0 0 1 1 1
0 0 1 1 1 1 1
1 0 1 0 0 1 1
0 0 1 1 1 1 1
1 1 1 0 0 1 1
0 1 0 1 1 1 1
0 0 0 0 1 1 1
0 1 0 1 1 1 1
0 1 1 0 0 1 1
0 1 0 1 1 1 1
1 0 0 0 1 1 1
0 1 0 1 1 1 1
1 1 1 0 0 1 1
0 1 1 0 0 1 1
0 0 1 0 0 1 1
0 1 1 0 0 1 1
0 0 1 1 1 1 1
0 1 1 0 0 1 1
0 1 0 1 1 1 1
0 1 1 0 0 1 1
1 0 1 0 0 1 1
0 1 1 1 1 1 1
0 0 0 0 1 1 1
0 1 1 1 1 1 1
0 0 1 0 0 1 1
0 1 1 1 1 1 1
1 0 0 0 1 1 1
0 1 1 1 1 1 1
1 0 1 0 0 1 1
1 0 0 0 0 1 1
1 0 0 0 1 1 1
1 0 0 0 0 1 1
1 0 1 0 0 1 1
1 0 0 0 0 1 1
1 1 1 0 0 1 1
1 0 0 0 1 1 1
0 0 0 0 1 1 1
1 0 0 0 1 1 1
0 0 0 1 1 1 1
1 0 0 0 1 1 1
0 0 1 1 1 1 1
1 0 0 0 1 1 1
0 1 0 1 1 1 1
1 0 0 0 1 1 1
0 1 1 1 1 1 1
1 0 0 0 1 1 1
1 0 0 0 0 1 1
1 0 0 0 1 1 1
1 0 1 0 0 1 1
1 0 0 0 1 1 1
1 1 1 0 0 1 1
1 0 1 0 0 1 1
0 0 1 0 0 1 1
1 0 1 0 0 1 1
0 0 1 1 1 1 1
1 0 1 0 0 1 1
0 1 1 0 0 1 1
1 0 1 0 0 1 1
0 1 1 1 1 1 1
1 0 1 0 0 1 1
1 0 0 0 0 1 1
1 0 1 0 0 1 1
1 0 0 0 1 1 1
1 1 1 0 0 1 1
0 0 1 0 0 1 1
1 1 1 0 0 1 1
0 0 1 1 1 1 1
1 1 1 0 0 1 1
0 1 0 1 1 1 1
1 1 1 0 0 1 1
1 0 0 0 0 1 1
1 1 1 0 0 1 1
1 0 0 0 1 1 1
*/
