// Digital circuit CP263_Lab_06_01_ALU.dig as structural Verilog
module CP263_Lab_06_01_ALU (
  input  [3:0] A,
  input  [3:0] B,
  input  M,
  input  [2:0] S,
  input  C,
  output [3:0] F,
  output Cout
);

  wire not_2_out;
  wire [3:0] Arithmetic, In01, In1, In02, In2, In03, In3, In04, In4, In05, In5, In06, In6, In7, Logical,
       not_3_out, not_4_out;

  assign In1 = ~A;  // Not not_1, 4 bits wide
  assign In2 = ~(A & B);  // NAnd nand_1, 4 bits wide
  assign In3 = ~(A | B);  // NOr nor_1, 4 bits wide
  assign In4 = ~(A ^ B);  // XNOr xnor_1, 4 bits wide
  assign In5 = A & B;  // And and_1, 4 bits wide
  assign In6 = A | B;  // Or or_1, 4 bits wide
  assign In7 = A & ~B;  // And and_2, 4 bits wide
  Multiplexer #(.Selector_Bits(3), .Bits(4)) multiplexer_1 (
    .sel(S), .in_0(In1), .in_1(In2), .in_2(In3), .in_3(In4), .in_4(In5), .in_5(In6), .in_6(In7), .in_7(A),
    .out(Logical));
  Add #(.Bits(4)) A_plus_C (.a(A), .b(4'b0000), .c_i(C), .s(In01));  // open: c_o
  Sub #(.Bits(4)) A_plus_C_1 (.a(A), .b(4'b0000), .c_i(not_2_out), .s(In02));  // open: c_o
  not not_2 (not_2_out, C);
  Add #(.Bits(4)) A_plus_B_plus_C (.a(A), .b(B), .c_i(C), .s(In03));  // open: c_o
  Add #(.Bits(4)) A_B_1_plus_C (.a(A), .b(not_3_out), .c_i(C), .s(In04));  // open: c_o
  assign not_3_out = ~B;  // Not not_3, 4 bits wide
  Add #(.Bits(4)) A_plus_C_1_2 (.a(not_4_out), .b(4'b0000), .c_i(C), .s(In05));  // open: c_o
  assign not_4_out = ~A;  // Not not_4, 4 bits wide
  Add #(.Bits(4)) B_plus_C (.a(4'b0000), .b(B), .c_i(C), .s(In06));  // open: c_o
  Multiplexer #(.Selector_Bits(3), .Bits(4)) multiplexer_2 (
    .sel(S), .in_0(In01), .in_1(In02), .in_2(In03), .in_3(In04), .in_4(In05), .in_5(In06),
    .in_6({A[2:0], 1'b0}), .in_7({1'b0, A[3:1]}), .out(Arithmetic));
  Multiplexer #(.Bits(4)) multiplexer_3 (.sel(M), .in_0(Logical), .in_1(Arithmetic), .out(F));

  assign Cout = 1'b0;

  // Other names for the same wires on the sheet: In07[3:1] = A[2:0]; In8[3:0] = A; In08[2:0] = A[3:1]

  // Notes on the sheet:
  //   4-Bit Adder
  //   A+C-1 = A+(-(-C) - 1)) = A+(-~C) = A-(~C)
  //   A-B-1+C = A+(-B-1)+C = A+~B+C
  //   -B = ~B + 1  -->  ~B = -B-1
  //   -A+C-1 = (-A-1)+C = ~A+C
  //   -A = ~A+1 --> ~A = -A-1
  //   Constant Values should be n-bits like n-bits Adder
endmodule
