// Digital circuit cp263_cedt_midterm_2024_01.dig as structural Verilog
module cp263_cedt_midterm_2024_01 (
  input  X1,
  input  X2,
  input  X3,
  input  X4,
  output Y
);

  wire and_1_out, and_2_out, not_1_out;

  not not_1 (not_1_out, X3);
  and and_1 (and_1_out, X1, not_1_out);
  and and_2 (and_2_out, X2, X3, X4);
  or or_1 (Y, and_1_out, and_2_out);

  // Notes on the sheet:
  //   Y1 = (X2&X3&X4) | (X1&!X3);
endmodule
