// Digital circuit cp263_cedt_midterm_2025_01.dig as structural Verilog
module cp263_cedt_midterm_2025_01 (
  input  X0,
  input  X1,
  input  X2,
  input  X3,
  output Y1
);

  wire and_1_out, and_2_out, and_3_out, not_1_out, not_2_out, not_3_out;

  not not_1 (not_1_out, X0);
  not not_2 (not_2_out, X1);
  not not_3 (not_3_out, X2);
  and and_1 (and_1_out, not_1_out, X1, X3);
  and and_2 (and_2_out, X0, not_3_out);
  and and_3 (and_3_out, not_2_out, X2, X3);
  or or_1 (Y1, and_1_out, and_2_out, and_3_out);

  // Notes on the sheet:
  //   Y1 = (X3&X1&!X0) | (X3&X2&!X1) | (!X2&X0);
  //   3-Input 
  //   AND Gate
  //   3-Input 
  //   OR Gate
endmodule
