// Digital circuit cp263_cedt_midterm_2025_02.dig as structural Verilog
module cp263_cedt_midterm_2025_02 (
  input  [3:0] X,
  output Z0,
  output Z3,
  output Z2,
  output Z1
);

  wire or_1_out, or_2_out, or_3_out, or_4_out, or_7_out, or_8_out, out0, out1, out2, out3, out4, out5, out6,
       out7, out8, out9, out10, out11, out12, out13, out14, out15;

  Decoder #(.Selector_Bits(4)) decoder_1 (
    .sel(X), .out_0(out0), .out_1(out1), .out_2(out2), .out_3(out3), .out_4(out4), .out_5(out5),
    .out_6(out6), .out_7(out7), .out_8(out8), .out_9(out9), .out_10(out10), .out_11(out11), .out_12(out12),
    .out_13(out13), .out_14(out14), .out_15(out15));
  or or_1 (or_1_out, out2, out3, out5);
  or or_2 (or_2_out, out7, out11, out13);
  or or_3 (or_3_out, out0, out3, out6);
  or or_4 (or_4_out, out9, out12, out15);
  or or_5 (Z3, or_1_out, or_2_out);
  or or_6 (Z1, or_3_out, or_4_out);
  or or_7 (or_7_out, out0, out2, out4, out6);
  or or_8 (or_8_out, out8, out10, out12, out14);
  or or_9 (Z0, out0, out5, out10, out15);
  or or_10 (Z2, or_7_out, or_8_out);

  // Notes on the sheet:
  //   Decoder
  //   - Why not Demultiplexer 
  //   bcz it needs to choose selector
  //   Circuit 1 : Is Prime Number
  //   - 1 is not prime number
  //   - 2 -> 0010
  //   - 3 -> 0011
  //   - 5 -> 0101
  //   - 7 -> 0111
  //   - 11 -> 1011
  //   - 13 -> 1101
  //   Circuit 3 : Divided by 3
  //   - 0 -> 0000
  //   - 3 -> 0101
  //   - 6 -> 0110
  //   - 9 -> 1001
  //   - 12 -> 1100
  //   - 15 -> 1111
  //   Circuit 2 : Divided by 2
  //   - 0 -> 0000
  //   - 2 -> 0010
  //   - 4 -> 0100
  //   - 6 -> 0110
  //   - 8 -> 1000
  //   - 10 -> 1010
  //   - 12 -> 1100
  //   - 14 -> 1110
  //   Circuit 4 : Divided by 5
  //   - 0 -> 0000
  //   - 5 -> 0101
  //   - 10 -> 1010
  //   - 15 -> 1111
endmodule

/* Test case Testcase:
X Z3 Z2 Z1 Z0
0 0 1 1 1
1 0 0 0 0
2 1 1 0 0
3 1 0 1 0
4 0 1 0 0
5 1 0 0 1
6 0 1 1 0
7 1 0 0 0
8 0 1 0 0
9 0 0 1 0
10 0 1 0 1
11 1 0 0 0
12 0 1 1 0
13 1 0 0 0
14 0 1 0 0
15 0 0 1 1
*/
