// Digital circuit cp263_cedt_midterm_2025_03.dig as structural Verilog
module cp263_cedt_midterm_2025_03 (
  input  SM,
  input  SN,
  input  TE,
  input  RA,
  input  AH,
  input  LI,
  input  MW,
  input  MF,
  output WP,
  output FD
);

  wire and_2_out, AutomateFertilize, AutomateWater, OpenFertilizeDispenser, or_1_out;

  and and_1 (AutomateFertilize, SN, ~SM, ~RA);  // And
  and and_2 (and_2_out, SM, ~RA, LI);  // And
  or or_1 (or_1_out, TE, AH);
  and and_3 (AutomateWater, and_2_out, or_1_out);
  or or_2 (WP, AutomateWater, MW);
  or or_3 (OpenFertilizeDispenser, AutomateFertilize, MF);
  and and_4 (FD, ~WP, OpenFertilizeDispenser);  // And

  // Other names for the same wires on the sheet: AirHumidity = AH; Light = LI; ManualFertilize = MF; ManualWater = MW;
  //   OpenWaterPump = WP; RainOrNot = RA; SoilMoisture = SM; SoilNutrient = SN; Temperature = TE

  // Notes on the sheet:
  //   Input & Output
  //   Automate Water
  //   Condition 
  //   - SM = 1 & RA = 0 & LI = 1
  //   - (AND MUST HAVE) TE = 1 | AH = 1
  //   Automate Fertilize
  //   Condition 
  //   - SN = 1 & SM = 0
  //   - (AND) RA = 0
  //   Mutual Exclusion (Limitation)
  //   Can directly connect to WP
  //   but for FD -> check ~WP and FD 
  //   bcz water have more priority than fertilize
  //   Manual Condition
endmodule

/* Test case Testset:
SM SN TE RA AH LI MW MF WP FD
0 0 0 0 0 0 0 0 0 0
1 0 1 0 0 1 0 0 1 0
1 0 0 0 1 1 0 0 1 0
1 0 0 0 0 1 0 0 0 0
1 0 1 1 0 1 0 0 0 0
1 0 1 0 0 0 0 0 0 0
0 0 1 0 0 1 0 0 0 0
0 1 0 0 0 0 0 0 0 1
1 1 0 0 0 0 0 0 0 0
0 1 0 1 0 0 0 0 0 0
0 0 0 1 0 0 1 0 1 0
1 0 0 1 0 0 0 1 0 1
0 0 0 0 0 0 1 1 1 0
0 1 0 0 0 0 1 0 1 0
1 0 1 0 0 1 0 1 1 0
*/
