// Digital circuit cp263_cp_midterm_2021_01.dig as structural Verilog
module cp263_cp_midterm_2021_01 (
  input  A0,
  input  A1,
  input  A2,
  input  B0,
  input  B1,
  input  B2,
  output Display
);

  wire [3:0] SumTwoNum;

  Add #(.Bits(3)) add_1 (.a({A2, A1, A0}), .b({B2, B1, B0}), .c_i(1'b0), .s(SumTwoNum[2:0]), .c_o(SumTwoNum[3]));
  Comparator #(.Bits(4)) comparator_1 (.a(SumTwoNum), .b(4'b0101), .gt(Display));  // open: eq, lt
  Seven_Seg_Hex seven_seg_hex_1 (.d({3'b000, Display}), .dp(1'b0));

  // Other names for the same wires on the sheet: numA[2:0] = {A2, A1, A0}; numB[2:0] = {B2, B1, B0}

  // Notes on the sheet:
  //   Student ID : 6730084521 , 5 = 8th Digit
  //   Check if num1 + num2 > 5
  //   3 bit
  //   4 bit
  //   Note : Maximum Possible Value = 7+7 = 14 
  //   So , Just create 4 bit Output from Adder 
  //   Note : X + X = X (Sum) +1 (Cout) bit Adder
  //   Note : Comparator returns 1 bit 
  //   So we need to convert to 4-bit to use 7Segment
endmodule

/* Test case Testset:
A2 A1 A0 B2 B1 B0 Display
0 0 0 0 0 0 0
0 0 0 1 0 1 0
0 0 0 1 1 0 1
0 0 1 1 0 0 0
0 0 1 1 0 1 1
0 1 0 0 1 1 0
0 1 0 1 0 0 1
0 1 1 0 1 0 0
0 1 1 0 1 1 1
1 0 0 0 0 1 0
1 0 0 0 1 0 1
1 0 1 0 0 0 0
1 0 1 0 0 1 1
1 1 0 0 0 0 1
1 1 1 0 0 0 1
0 0 0 1 1 1 1
1 0 0 1 0 0 1
1 1 1 1 1 1 1
*/
