// Digital circuit cp263_cp_midterm_2021_02.dig as structural Verilog
module cp263_cp_midterm_2021_02 (
  input  S0,
  input  S1,
  input  S2
);

  wire or_1_out, or_2_out, out0, out1, out2, out3, out4, out5, out6, out7;

  Decoder #(.Selector_Bits(3)) decoder_1 (
    .sel({S0, S1, S2}), .out_0(out0), .out_1(out1), .out_2(out2), .out_3(out3), .out_4(out4), .out_5(out5),
    .out_6(out6), .out_7(out7));
  or or_1 (or_1_out, out2, out4, out5, out6);
  or or_2 (or_2_out, out0, out2, out4, out6, out7);
  // Probe O1 on or_1_out
  // Probe O2 on or_2_out

  // Notes on the sheet:
  //   Note : Only connect with Output 1
endmodule
