// Digital circuit cp263_cp_midterm_2023_02.dig as structural Verilog
module cp263_cp_midterm_2023_02 (
  input  [7:0] in0,
  input  [7:0] in1,
  input  addsubtract,
  output [4:0] out
);

  wire [1:0] add_1_c_o, add_2_s, add_3_s, add_4_s, add_5_s, add_6_s, add_7_s, add_8_s, add_9_s, add_10_s,
       add_11_s, add_12_s;
  wire [2:2] add_9_c_o, add_10_c_o, add_11_c_o, add_12_c_o;
  wire [3:0] CountOne_0, CountOne_1;
  wire [4:0] Add, Sub;

  Add add_1 (.a(in0[0]), .b(in0[1]), .c_i(1'b0), .s(add_1_c_o[0]), .c_o(add_1_c_o[1]));
  Add add_2 (.a(in0[2]), .b(in0[3]), .c_i(1'b0), .s(add_2_s[0]), .c_o(add_2_s[1]));
  Add add_3 (.a(in0[4]), .b(in0[5]), .c_i(1'b0), .s(add_3_s[0]), .c_o(add_3_s[1]));
  Add add_4 (.a(in0[6]), .b(in0[7]), .c_i(1'b0), .s(add_4_s[0]), .c_o(add_4_s[1]));
  Add add_5 (.a(in1[0]), .b(in1[1]), .c_i(1'b0), .s(add_5_s[0]), .c_o(add_5_s[1]));
  Add add_6 (.a(in1[2]), .b(in1[3]), .c_i(1'b0), .s(add_6_s[0]), .c_o(add_6_s[1]));
  Add add_7 (.a(in1[4]), .b(in1[5]), .c_i(1'b0), .s(add_7_s[0]), .c_o(add_7_s[1]));
  Add add_8 (.a(in1[6]), .b(in1[7]), .c_i(1'b0), .s(add_8_s[0]), .c_o(add_8_s[1]));
  Add #(.Bits(2)) add_9 (.a(add_1_c_o), .b(add_2_s), .c_i(1'b0), .s(add_9_s), .c_o(add_9_c_o[2]));
  Add #(.Bits(2)) add_10 (.a(add_3_s), .b(add_4_s), .c_i(1'b0), .s(add_10_s), .c_o(add_10_c_o[2]));
  Add #(.Bits(2)) add_11 (.a(add_5_s), .b(add_6_s), .c_i(1'b0), .s(add_11_s), .c_o(add_11_c_o[2]));
  Add #(.Bits(2)) add_12 (.a(add_7_s), .b(add_8_s), .c_i(1'b0), .s(add_12_s), .c_o(add_12_c_o[2]));
  Add #(.Bits(3)) add_13 (
    .a({add_9_c_o[2], add_9_s}), .b({add_10_c_o[2], add_10_s}), .c_i(1'b0), .s(CountOne_0[2:0]),
    .c_o(CountOne_0[3]));
  Add #(.Bits(3)) add_14 (
    .a({add_11_c_o[2], add_11_s}), .b({add_12_c_o[2], add_12_s}), .c_i(1'b0), .s(CountOne_1[2:0]),
    .c_o(CountOne_1[3]));
  Add #(.Bits(4)) add_15 (.a(CountOne_0), .b(CountOne_1), .c_i(1'b0), .s(Add[3:0]), .c_o(Add[4]));
  Sub #(.Bits(4)) sub_1 (.a(CountOne_0), .b(CountOne_1), .c_i(1'b0), .s(Sub[3:0]), .c_o(Sub[4]));
  Multiplexer #(.Bits(5)) multiplexer_1 (.sel(addsubtract), .in_0(Add), .in_1(Sub), .out(out));

  // Other names for the same wires on the sheet: ast = addsubtract

  // Notes on the sheet:
  //   Note : Splitter 1bit -> 2 bit with same value
  //   splitter having job of split/merge bit
  //   1-bit Adder -> 2-bit Adder -> 4-bit Adder
  //     1 to 2 bit    ->   2 to 3 bit  -> 3 to 4 bit
  //   1-bit Adder -> 2-bit Adder -> 4-bit Adder
  //     1 to 2 bit    ->   2 to 4 bit  -> 4 to 8 bit
  //   4 bit + 4 bit -> 4 bit sum + 1 bit Cout
  //   but merge with Cout -> get 5 bit as result
endmodule
