// Digital circuit cp_2024_01.dig as structural Verilog
module cp_2024_01 (
  input  [3:0] in,
  output out2,
  output out1
);

  wire and_1_out, and_2_out, and_3_out, and_4_out, and_5_out, and_6_out, and_7_out, not_1_out, not_2_out,
       not_3_out, not_4_out, not_5_out, not_6_out, not_7_out;

  not not_1 (not_1_out, in[0]);
  not not_2 (not_2_out, in[1]);
  not not_3 (not_3_out, in[2]);
  and and_1 (and_1_out, not_1_out, in[1], not_3_out);
  and and_2 (and_2_out, not_1_out, in[1], in[3]);
  and and_3 (and_3_out, in[0], not_2_out);
  or or_1 (out1, and_1_out, and_2_out, and_3_out);
  not not_4 (not_4_out, in[0]);
  not not_5 (not_5_out, in[1]);
  not not_6 (not_6_out, in[2]);
  not not_7 (not_7_out, in[3]);
  and and_4 (and_4_out, not_4_out, in[2], not_7_out);
  and and_5 (and_5_out, in[0], in[1]);
  and and_6 (and_6_out, not_4_out, not_5_out);
  and and_7 (and_7_out, not_5_out, not_6_out, in[3]);
  or or_2 (out2, and_4_out, and_5_out, and_6_out, and_7_out);

  // Notes on the sheet:
  //   Out1 = (!In2&In1&!In0) | (In3&In1&!In0) | (!In1&In0);
  //   Out2 = (!In3&In2&!In0) | (In3&!In2&!In1) | (In1&In0) | (!In1&!In0);
endmodule

/* Test case Testset:
In3 In2 In1 In0 out1 out2
0 0 0 0 0 1 
0 0 0 1 1 0
0 0 1 0 1 0
0 0 1 1 0 1
0 1 0 0 0 1
0 1 0 1 1 0
0 1 1 0 0 1
0 1 1 1 0 1
1 0 0 0 0 1
1 0 0 1 1 1
1 0 1 0 1 0
1 0 1 1 0 1
1 1 0 0 0 1
1 1 0 1 1 0
1 1 1 0 1 0
1 1 1 1 0 1
*/
