// Digital circuit cp263_cp_midterm_2024_02.dig as structural Verilog
module cp263_cp_midterm_2024_02 (
  input  [7:0] Input,
  output [2:0] Output
);

  wire meeonemai;
  wire [2:0] difference, leftpos, R2L_num, rightpos;

  PriorityEncoder #(.Selector_Bits(3)) L2R (
    .in0(Input[0]), .in1(Input[1]), .in2(Input[2]), .in3(Input[3]), .in4(Input[4]), .in5(Input[5]),
    .in6(Input[6]), .in7(Input[7]), .num(leftpos), .any(meeonemai));
  PriorityEncoder #(.Selector_Bits(3)) R2L (
    .in0(Input[7]), .in1(Input[6]), .in2(Input[5]), .in3(Input[4]), .in4(Input[3]), .in5(Input[2]),
    .in6(Input[1]), .in7(Input[0]), .num(R2L_num));  // open: any
  Multiplexer #(.Bits(3)) multiplexer_1 (.sel(meeonemai), .in_0(3'b000), .in_1(difference), .out(Output));
  Sub #(.Bits(3)) _7_P_0 (.a(3'b111), .b(R2L_num), .c_i(1'b0), .s(rightpos));  // open: c_o
  Sub #(.Bits(3)) L_R_0 (.a(leftpos), .b(rightpos), .c_i(1'b0), .s(difference));  // open: c_o

  // Other names for the same wires on the sheet: In0 = Input[0]; In1 = Input[1]; In2 = Input[2]; In3 = Input[3];
  //   In4 = Input[4]; In5 = Input[5]; In6 = Input[6]; In7 = Input[7]

  // Notes on the sheet:
  //   Finding 1 Algorithm 
  //   With Priority Encoder
  //   --> 3 bit out
  //   Find Difference (for Output)
endmodule

/* Test case Testcase:
Input Output
0 0
1 0
2 0
3 1
5 2
6 1
9 3
15 3
64 0
69 6
128 0
129 7
192 1
254 6
255 7
*/
