// Digital circuit cp263_cp_midterm_2025_02.dig as structural Verilog
module cp263_cp_midterm_2025_02 (
  input  [7:0] in,
  output [3:0] out
);

  wire having0;
  wire [2:0] _7_C_0_s, L2R_num, R2L_num;
  wire [3:0] calculated;

  PriorityEncoder #(.Selector_Bits(3)) L2R (
    .in0(in[0]), .in1(in[1]), .in2(in[2]), .in3(in[3]), .in4(in[4]), .in5(in[5]), .in6(in[6]), .in7(in[7]),
    .num(L2R_num), .any(having0));
  PriorityEncoder #(.Selector_Bits(3)) R2L (
    .in0(in[7]), .in1(in[6]), .in2(in[5]), .in3(in[4]), .in4(in[3]), .in5(in[2]), .in6(in[1]), .in7(in[0]),
    .num(R2L_num), .any(having0));
  Sub #(.Bits(3)) _7_C_0 (.a(3'b111), .b(R2L_num), .c_i(1'b0), .s(_7_C_0_s));  // open: c_o
  Multiplexer #(.Bits(4)) multiplexer_1 (.sel(having0), .in_0(4'b0000), .in_1(calculated), .out(out));
  Add #(.Bits(3)) add_1 (.a(L2R_num), .b(_7_C_0_s), .c_i(1'b0), .s(calculated[2:0]), .c_o(calculated[3]));

  // Notes on the sheet:
  //   For Logic of Checking 0000 0000 -> use "any" to check 
  //   "any" will return 0 if bit 1 wasn't found
  //   Note : Priority Encoder still find MSB (InX when X is most value)
  //   so reversing input didnt help --> fix by using subtractor
  //   Note : Input X bit + Input X bit -> X bit output 
  //   We need to merge 1 bit from C_out to be X+1 bit
  //   Note : MUX acts like IF
  //   if select 0 (any) -> return 0
  //   else if select 1 (any) -> return calculated value
endmodule

/* Test case Basic testcase:
in out
69 6
64 12
0 0
6 3
*/
