// Digital circuit cp263_cp_midterm_example_01.dig as structural Verilog
module cp263_cp_midterm_example_01 (
  input  I0,
  input  I1,
  input  I2
);

  wire and_1_out, and_2_out, and_3_out, and_4_out, Out1, Out2;

  and and_1 (and_1_out, ~I0, I1);  // And
  and and_2 (and_2_out, I0, ~I1);  // And
  and and_3 (and_3_out, ~I1, I2);  // And
  and and_4 (and_4_out, I1, ~I2);  // And
  or or_1 (Out1, and_1_out, and_2_out);
  or or_2 (Out2, and_3_out, and_4_out);
  // Probe O0 on I0
  // Probe O1 on Out1
  // Probe O2 on Out2

  // Other names for the same wires on the sheet: In1 = I1; In2 = I2; In0 = I0; Out0 = I0
endmodule

/* Test case Testset:
I0 I1 I2 O0 O1 O2
0 0 0 0 0 0
0 0 1 0 0 1
0 1 0 0 1 1
0 1 1 0 1 0
1 0 0 1 1 0
1 0 1 1 1 1
1 1 0 1 0 1
1 1 1 1 0 0
*/
