// Digital circuit cp263_cp_midterm_example_ii.dig as structural Verilog
module cp263_cp_midterm_example_ii (
  input  A1,
  input  A2,
  input  A3,
  input  A4,
  input  A5,
  input  B1,
  input  B2,
  input  B3
);

  wire ResultA, ResultB, SameVote;
  wire [2:0] A1_plus_A2_plus_0_s, A1_plus_A2_plus_A3_plus_A4_s, A1_plus_A2_plus_A3_s, B1_plus_B2_s,
       VoteGroupA, VoteGroupB;

  Comparator #(.Bits(3)) CompareA (.a(VoteGroupA), .b(3'b010), .gt(ResultA));  // open: eq, lt
  Comparator #(.Bits(3)) CompareB (.a(VoteGroupB), .b(3'b001), .gt(ResultB));  // open: eq, lt
  Add #(.Bits(3)) A1_plus_A2_plus_0 (
    .a({2'b00, A1}), .b({2'b00, A2}), .c_i(1'b0), .s(A1_plus_A2_plus_0_s));  // open: c_o
  Add #(.Bits(3)) A1_plus_A2_plus_A3 (
    .a(A1_plus_A2_plus_0_s), .b({2'b00, A3}), .c_i(1'b0), .s(A1_plus_A2_plus_A3_s));  // open: c_o
  Add #(.Bits(3)) A1_plus_A2_plus_A3_plus_A4 (
    .a(A1_plus_A2_plus_A3_s), .b({2'b00, A4}), .c_i(1'b0), .s(A1_plus_A2_plus_A3_plus_A4_s));  // open: c_o
  Add #(.Bits(3)) A1_plus_A2_plus_A3_plus_A4_plus_A5 (
    .a(A1_plus_A2_plus_A3_plus_A4_s), .b({2'b00, A5}), .c_i(1'b0), .s(VoteGroupA));  // open: c_o
  xnor xnor_1 (SameVote, ResultA, ResultB);
  Add #(.Bits(3)) B1_plus_B2 (.a({2'b00, B1}), .b({2'b00, B2}), .c_i(1'b0), .s(B1_plus_B2_s));  // open: c_o
  Add #(.Bits(3)) B1_plus_B2_plus_B3 (.a(B1_plus_B2_s), .b({2'b00, B3}), .c_i(1'b0), .s(VoteGroupB));  // open: c_o
  // Probe RA on ResultA
  // Probe RB on ResultB
  // Probe SV on SameVote

  // Other names for the same wires on the sheet: A1_t[0] = A1; A2_t[0] = A2; A3_t[0] = A3; A4_t[0] = A4; A5_t[0] = A5;
  //   B1_t[0] = B1; B2_t[0] = B2; B3_t[0] = B3

  // Notes on the sheet:
  //   Note : to win , vote must more than half
  //   so 
  //   - In group of 5 : vote must > 2 to win
  //   - In group of 3 , vote must > 1 to win
  //   Step 1 : Compare Votes in two groups
  //   By using comparator
  //   Note : We can use Adder Layer to sum all value
  //   Max Vote = 1 (x5) , So we expand to 3 bit Adder
  //   Step 2 : Compare Sum of Voting 1
  //   Whether it's more than half
  //   - If Vote1 > half -> 1 Win
  //   - Else Vote 1 < half -> 0 Win
  //   Group of 5 
  //   (Group A)
  //   Group of 3 
  //   (Group B)
  //   X --> 00X (1 bit => 3 bit)
  //   Output 1 Bit
  //   Step 3 : Check If Vote Same (By XNOR)
  //   Step 4 : Show Result
endmodule

/* Test case 256 Testcase:
A1 A2 A3 A4 A5 B1 B2 B3 RA RB SV
0 0 0 0 0 0 0 0 0 0 1
0 0 0 0 0 0 0 1 0 0 1
0 0 0 0 0 0 1 0 0 0 1
0 0 0 0 0 0 1 1 0 1 0
0 0 0 0 0 1 0 0 0 0 1
0 0 0 0 0 1 0 1 0 1 0
0 0 0 0 0 1 1 0 0 1 0
0 0 0 0 0 1 1 1 0 1 0
0 0 0 0 1 0 0 0 0 0 1
0 0 0 0 1 0 0 1 0 0 1
0 0 0 0 1 0 1 0 0 0 1
0 0 0 0 1 0 1 1 0 1 0
0 0 0 0 1 1 0 0 0 0 1
0 0 0 0 1 1 0 1 0 1 0
0 0 0 0 1 1 1 0 0 1 0
0 0 0 0 1 1 1 1 0 1 0
0 0 0 1 0 0 0 0 0 0 1
0 0 0 1 0 0 0 1 0 0 1
0 0 0 1 0 0 1 0 0 0 1
0 0 0 1 0 0 1 1 0 1 0
0 0 0 1 0 1 0 0 0 0 1
0 0 0 1 0 1 0 1 0 1 0
0 0 0 1 0 1 1 0 0 1 0
0 0 0 1 0 1 1 1 0 1 0
0 0 0 1 1 0 0 0 0 0 1
0 0 0 1 1 0 0 1 0 0 1
0 0 0 1 1 0 1 0 0 0 1
0 0 0 1 1 0 1 1 0 1 0
0 0 0 1 1 1 0 0 0 0 1
0 0 0 1 1 1 0 1 0 1 0
0 0 0 1 1 1 1 0 0 1 0
0 0 0 1 1 1 1 1 0 1 0
0 0 1 0 0 0 0 0 0 0 1
0 0 1 0 0 0 0 1 0 0 1
0 0 1 0 0 0 1 0 0 0 1
0 0 1 0 0 0 1 1 0 1 0
0 0 1 0 0 1 0 0 0 0 1
0 0 1 0 0 1 0 1 0 1 0
0 0 1 0 0 1 1 0 0 1 0
0 0 1 0 0 1 1 1 0 1 0
0 0 1 0 1 0 0 0 0 0 1
0 0 1 0 1 0 0 1 0 0 1
0 0 1 0 1 0 1 0 0 0 1
0 0 1 0 1 0 1 1 0 1 0
0 0 1 0 1 1 0 0 0 0 1
0 0 1 0 1 1 0 1 0 1 0
0 0 1 0 1 1 1 0 0 1 0
0 0 1 0 1 1 1 1 0 1 0
0 0 1 1 0 0 0 0 0 0 1
0 0 1 1 0 0 0 1 0 0 1
0 0 1 1 0 0 1 0 0 0 1
0 0 1 1 0 0 1 1 0 1 0
0 0 1 1 0 1 0 0 0 0 1
0 0 1 1 0 1 0 1 0 1 0
0 0 1 1 0 1 1 0 0 1 0
0 0 1 1 0 1 1 1 0 1 0
0 0 1 1 1 0 0 0 1 0 0
0 0 1 1 1 0 0 1 1 0 0
0 0 1 1 1 0 1 0 1 0 0
0 0 1 1 1 0 1 1 1 1 1
0 0 1 1 1 1 0 0 1 0 0
0 0 1 1 1 1 0 1 1 1 1
0 0 1 1 1 1 1 0 1 1 1
0 0 1 1 1 1 1 1 1 1 1
0 1 0 0 0 0 0 0 0 0 1
0 1 0 0 0 0 0 1 0 0 1
0 1 0 0 0 0 1 0 0 0 1
0 1 0 0 0 0 1 1 0 1 0
0 1 0 0 0 1 0 0 0 0 1
0 1 0 0 0 1 0 1 0 1 0
0 1 0 0 0 1 1 0 0 1 0
0 1 0 0 0 1 1 1 0 1 0
0 1 0 0 1 0 0 0 0 0 1
0 1 0 0 1 0 0 1 0 0 1
0 1 0 0 1 0 1 0 0 0 1
0 1 0 0 1 0 1 1 0 1 0
0 1 0 0 1 1 0 0 0 0 1
0 1 0 0 1 1 0 1 0 1 0
0 1 0 0 1 1 1 0 0 1 0
0 1 0 0 1 1 1 1 0 1 0
0 1 0 1 0 0 0 0 0 0 1
0 1 0 1 0 0 0 1 0 0 1
0 1 0 1 0 0 1 0 0 0 1
0 1 0 1 0 0 1 1 0 1 0
0 1 0 1 0 1 0 0 0 0 1
0 1 0 1 0 1 0 1 0 1 0
0 1 0 1 0 1 1 0 0 1 0
0 1 0 1 0 1 1 1 0 1 0
0 1 0 1 1 0 0 0 1 0 0
0 1 0 1 1 0 0 1 1 0 0
0 1 0 1 1 0 1 0 1 0 0
0 1 0 1 1 0 1 1 1 1 1
0 1 0 1 1 1 0 0 1 0 0
0 1 0 1 1 1 0 1 1 1 1
0 1 0 1 1 1 1 0 1 1 1
0 1 0 1 1 1 1 1 1 1 1
0 1 1 0 0 0 0 0 0 0 1
0 1 1 0 0 0 0 1 0 0 1
0 1 1 0 0 0 1 0 0 0 1
0 1 1 0 0 0 1 1 0 1 0
0 1 1 0 0 1 0 0 0 0 1
0 1 1 0 0 1 0 1 0 1 0
0 1 1 0 0 1 1 0 0 1 0
0 1 1 0 0 1 1 1 0 1 0
0 1 1 0 1 0 0 0 1 0 0
0 1 1 0 1 0 0 1 1 0 0
0 1 1 0 1 0 1 0 1 0 0
0 1 1 0 1 0 1 1 1 1 1
0 1 1 0 1 1 0 0 1 0 0
0 1 1 0 1 1 0 1 1 1 1
0 1 1 0 1 1 1 0 1 1 1
0 1 1 0 1 1 1 1 1 1 1
0 1 1 1 0 0 0 0 1 0 0
0 1 1 1 0 0 0 1 1 0 0
0 1 1 1 0 0 1 0 1 0 0
0 1 1 1 0 0 1 1 1 1 1
0 1 1 1 0 1 0 0 1 0 0
0 1 1 1 0 1 0 1 1 1 1
0 1 1 1 0 1 1 0 1 1 1
0 1 1 1 0 1 1 1 1 1 1
0 1 1 1 1 0 0 0 1 0 0
0 1 1 1 1 0 0 1 1 0 0
0 1 1 1 1 0 1 0 1 0 0
0 1 1 1 1 0 1 1 1 1 1
0 1 1 1 1 1 0 0 1 0 0
0 1 1 1 1 1 0 1 1 1 1
0 1 1 1 1 1 1 0 1 1 1
0 1 1 1 1 1 1 1 1 1 1
1 0 0 0 0 0 0 0 0 0 1
1 0 0 0 0 0 0 1 0 0 1
1 0 0 0 0 0 1 0 0 0 1
1 0 0 0 0 0 1 1 0 1 0
1 0 0 0 0 1 0 0 0 0 1
1 0 0 0 0 1 0 1 0 1 0
1 0 0 0 0 1 1 0 0 1 0
1 0 0 0 0 1 1 1 0 1 0
1 0 0 0 1 0 0 0 0 0 1
1 0 0 0 1 0 0 1 0 0 1
1 0 0 0 1 0 1 0 0 0 1
1 0 0 0 1 0 1 1 0 1 0
1 0 0 0 1 1 0 0 0 0 1
1 0 0 0 1 1 0 1 0 1 0
1 0 0 0 1 1 1 0 0 1 0
1 0 0 0 1 1 1 1 0 1 0
1 0 0 1 0 0 0 0 0 0 1
1 0 0 1 0 0 0 1 0 0 1
1 0 0 1 0 0 1 0 0 0 1
1 0 0 1 0 0 1 1 0 1 0
1 0 0 1 0 1 0 0 0 0 1
1 0 0 1 0 1 0 1 0 1 0
1 0 0 1 0 1 1 0 0 1 0
1 0 0 1 0 1 1 1 0 1 0
1 0 0 1 1 0 0 0 1 0 0
1 0 0 1 1 0 0 1 1 0 0
1 0 0 1 1 0 1 0 1 0 0
1 0 0 1 1 0 1 1 1 1 1
1 0 0 1 1 1 0 0 1 0 0
1 0 0 1 1 1 0 1 1 1 1
1 0 0 1 1 1 1 0 1 1 1
1 0 0 1 1 1 1 1 1 1 1
1 0 1 0 0 0 0 0 0 0 1
1 0 1 0 0 0 0 1 0 0 1
1 0 1 0 0 0 1 0 0 0 1
1 0 1 0 0 0 1 1 0 1 0
1 0 1 0 0 1 0 0 0 0 1
1 0 1 0 0 1 0 1 0 1 0
1 0 1 0 0 1 1 0 0 1 0
1 0 1 0 0 1 1 1 0 1 0
1 0 1 0 1 0 0 0 1 0 0
1 0 1 0 1 0 0 1 1 0 0
1 0 1 0 1 0 1 0 1 0 0
1 0 1 0 1 0 1 1 1 1 1
1 0 1 0 1 1 0 0 1 0 0
1 0 1 0 1 1 0 1 1 1 1
1 0 1 0 1 1 1 0 1 1 1
1 0 1 0 1 1 1 1 1 1 1
1 0 1 1 0 0 0 0 1 0 0
1 0 1 1 0 0 0 1 1 0 0
1 0 1 1 0 0 1 0 1 0 0
1 0 1 1 0 0 1 1 1 1 1
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*/
